# Fritzing sketch Remote Control (saved by Fritzing 0.9.1b)
circuit board: 6.64626cm x 5.36222cm
breadboards: 1

parts:
  S2 = Pushbutton [package="[THT]"]
  S3 = Pushbutton [package="[THT]"]
  S4 = Pushbutton [package="[THT]"]
  R1 = Resistor [tolerance=±5% resistance=1k package=THT]
  R2 = Resistor [tolerance=±5% resistance=1k package=THT]
  R3 = Resistor [tolerance=±5% resistance=1k package=THT]
  U1 = XBee
  R4 = Rotary Potentiometer (Small) [maximum_resistance=100kΩ package=THT]
  Parte1 = Arduino Uno (Rev3)
  R5 = Resistor [tolerance=±5% resistance=220 package=THT]
  R6 = Resistor [tolerance=±5% resistance=120 package=THT]
  LED3 = DUO LED RG [package="5 mm [THT]"]

nets:
  GND: S2.Pin_1, S2.Pin_2, S3.Pin_1, S3.Pin_2, S4.Pin_1, S4.Pin_2, U1.GND, R4.leg1, Parte1.GND, LED3.common_cathode
  N1: S2.Pin_3, S2.Pin_4, R3.Pin_1, Parte1.D4
  N2: S3.Pin_3, S3.Pin_4, R2.Pin_1, Parte1.D3_PWM
  N3: S4.Pin_3, S4.Pin_4, R1.Pin_1, Parte1.D2
  N4: R1.Pin_0, R2.Pin_0, R3.Pin_0, Parte1.5V
  VCC: U1.VCC, Parte1.3V3
  N5: U1.pin2, Parte1.D0/RX
  N6: U1.pin3, Parte1.D1/TX
  N7: R4.wiper, Parte1.A0
  N8: R4.leg2, Parte1.VIN
  N9: Parte1.D10_PWM/SS, R5.Pin_1
  N10: Parte1.D11_PWM/MOSI, R6.Pin_1
  N11: R5.Pin_0, LED3.red_anode
  N12: R6.Pin_0, LED3.green_anode
